// Logisim project 2006 6.circ as structural Verilog: 1 circuit, main circuit main
module main (
  input  in_1,
  input  in_2,
  output NOTA_10,
  output NOTA_7,
  output NOTA_5
);

  wire and_1_out, clock_1_out, clock_2_out, d_ff_1_q, d_ff_2_q, d_ff_3_q, t_ff_1_q, t_ff_2_q;

  Clock clock_1 (.out(clock_1_out));
  Clock clock_2 (.out(clock_2_out));
  D_Flip_Flop d_ff_1 (.clk(clock_2_out), .D(in_1), .Q(d_ff_1_q));  // open: Qn, preset, en, reset
  T_Flip_Flop t_ff_1 (.clk(clock_2_out), .T(in_2), .Q(t_ff_1_q), .reset(and_1_out));  // open: Qn, preset, en
  D_Flip_Flop d_ff_2 (.clk(clock_2_out), .D(d_ff_1_q), .Q(d_ff_2_q));  // open: Qn, preset, en, reset
  T_Flip_Flop t_ff_2 (.clk(clock_2_out), .T(t_ff_1_q), .Q(t_ff_2_q), .reset(and_1_out));  // open: Qn, preset, en
  D_Flip_Flop d_ff_3 (.clk(clock_2_out), .D(d_ff_2_q), .Q(d_ff_3_q));  // open: Qn, preset, en, reset
  and and_1 (and_1_out, t_ff_1_q, t_ff_2_q);
  and and_2 (NOTA_10, d_ff_1_q, d_ff_2_q, t_ff_2_q, d_ff_3_q);
  and and_3 (NOTA_7, ~d_ff_1_q, d_ff_2_q, d_ff_3_q, t_ff_2_q);  // AND_Gate
  and and_4 (NOTA_5, ~d_ff_1_q, ~d_ff_2_q, d_ff_3_q, t_ff_2_q);  // AND_Gate
endmodule
