// Logisim project 2021 1 SIN ACABAR.circ as structural Verilog: 1 circuit, main circuit main
module main (
  input  RES,
  input  PRE,
  input  A1,
  input  A2,
  input  A3,
  input  in_6
);

  wire and_1_out, and_2_out, and_4_out, and_5_out, and_7_out, clock_1_out, j_k_ff_1_q, j_k_ff_2_q, or_1_out,
       or_2_out, or_3_out;

  Clock clock_1 (.out(clock_1_out));
  and and_1 (and_1_out, A1, PRE);
  J_K_Flip_Flop j_k_ff_1 (
    .J(1'b1), .clk(clock_1_out), .K(1'b1), .Q(j_k_ff_1_q), .preset(and_1_out), .reset(or_1_out));  // open: Qn, en
  or or_1 (or_1_out, and_2_out, RES);
  and and_2 (and_2_out, ~A1, PRE);  // AND_Gate
  // AND_Gate and_3 has open pins: in0=A2, in1=PRE, out=open
  and and_4 (and_4_out, ~A2, PRE);  // AND_Gate
  J_K_Flip_Flop j_k_ff_2 (
    .J(j_k_ff_1_q), .clk(clock_1_out), .K(j_k_ff_1_q), .Q(j_k_ff_2_q), .reset(or_2_out));  // open: Qn, preset, en
  or or_2 (or_2_out, and_4_out, RES);
  and and_5 (and_5_out, j_k_ff_1_q, j_k_ff_2_q);
  J_K_Flip_Flop j_k_ff_3 (
    .J(and_5_out), .clk(clock_1_out), .K(and_5_out), .reset(or_3_out));  // open: Q, Qn, preset, en
  or or_3 (or_3_out, and_7_out, RES);
  // AND_Gate and_6 has open pins: in0=A3, in1=in_6, out=open
  and and_7 (and_7_out, ~A3, in_6);  // AND_Gate
endmodule
