// Logisim project 2021 2.circ as structural Verilog: 1 circuit, main circuit main
module main (
  input  in_1,
  output out_2,
  output out_3,
  output out_4,
  output out_5
);

  wire and_1_out, and_2_out, and_3_out, and_4_out, and_5_out, and_6_out, and_7_out, and_8_out, clock_1_out,
       or_1_out, or_2_out, or_3_out, t_ff_1_qn;

  Clock clock_1 (.out(clock_1_out));
  and and_1 (and_1_out, ~in_1, ~out_5, ~out_4);  // AND_Gate
  and and_2 (and_2_out, out_4, out_5);
  or or_1 (or_1_out, and_1_out, and_2_out, out_3);
  T_Flip_Flop t_ff_1 (.clk(clock_1_out), .T(or_1_out), .Q(out_5), .Qn(t_ff_1_qn));  // open: preset, reset, en
  and and_3 (and_3_out, in_1, ~out_4);  // AND_Gate
  and and_4 (and_4_out, out_4, ~in_1);  // AND_Gate
  or or_2 (or_2_out, and_3_out, and_4_out);
  and and_5 (and_5_out, ~in_1, out_4);  // AND_Gate
  and and_6 (and_6_out, ~out_4, out_3);  // AND_Gate
  T_Flip_Flop t_ff_2 (.clk(clock_1_out), .T(or_2_out), .Q(out_4));  // open: Qn, preset, reset, en
  or or_3 (or_3_out, and_5_out, and_6_out);
  T_Flip_Flop t_ff_3 (.clk(clock_1_out), .T(or_3_out), .Q(out_3));  // open: Qn, preset, reset, en
  and and_7 (and_7_out, ~in_1, out_5, out_4);  // AND_Gate
  and and_8 (and_8_out, in_1, out_3);
  or or_4 (out_2, and_7_out, and_8_out);
endmodule
