// Logisim project 2022 3 arreglado.circ as structural Verilog: 1 circuit, main circuit main
module main (
  input  A0,
  input  A1,
  input  A2,
  input  L
);

  wire _6_out, and_1_out, and_2_out, and_3_out, and_4_out, and_5_out, and_6_out, and_7_out, and_8_out,
       and_9_out, clock_1_out, j_k_ff_1_q, j_k_ff_1_qn, j_k_ff_2_q, j_k_ff_3_q, nand_1_out, nand_2_out,
       or_1_out, or_2_out, or_3_out, or_4_out;

  Clock clock_1 (.out(clock_1_out));
  nand nand_1 (nand_1_out, ~A0, L);  // NAND_Gate
  nand nand_2 (nand_2_out, A0, L);
  J_K_Flip_Flop j_k_ff_1 (
    .J(and_1_out), .clk(clock_1_out), .K(nand_2_out), .Q(j_k_ff_1_q), .Qn(j_k_ff_1_qn));  // open: preset, en, reset
  and and_1 (and_1_out, nand_1_out, ~_6_out);  // AND_Gate
  and and_2 (and_2_out, ~L, j_k_ff_1_q);  // AND_Gate
  and and_3 (and_3_out, A1, L);
  and _6 (_6_out, j_k_ff_1_qn, ~L, j_k_ff_2_q, j_k_ff_3_q);  // AND_Gate
  or or_1 (or_1_out, and_2_out, and_3_out);
  and and_4 (and_4_out, j_k_ff_1_q, ~L);  // AND_Gate
  and and_5 (and_5_out, ~A1, L);  // AND_Gate
  J_K_Flip_Flop j_k_ff_2 (
    .J(or_1_out), .clk(clock_1_out), .K(or_2_out), .Q(j_k_ff_2_q));  // open: Qn, preset, en, reset
  or or_2 (or_2_out, and_4_out, _6_out, and_5_out);
  and and_6 (and_6_out, ~L, j_k_ff_1_q, j_k_ff_2_q);  // AND_Gate
  and and_7 (and_7_out, L, A2);
  and and_8 (and_8_out, j_k_ff_2_q, ~L);  // AND_Gate
  and and_9 (and_9_out, ~A2, L);  // AND_Gate
  or or_3 (or_3_out, and_6_out, and_7_out);
  or or_4 (or_4_out, and_8_out, _6_out, and_9_out);
  J_K_Flip_Flop j_k_ff_3 (
    .J(or_3_out), .clk(clock_1_out), .K(or_4_out), .Q(j_k_ff_3_q));  // open: Qn, preset, en, reset
endmodule
