// Logisim project 2022 3.circ as structural Verilog: 1 circuit, main circuit main
module main (
  input  A2,
  input  A1,
  input  A0,
  input  L,
  output out_5
);

  wire and_1_out, and_3_out, and_4_out, and_5_out, and_6_out, and_7_out, and_8_out, clock_1_out, j_k_ff_1_q,
       j_k_ff_2_q, nand_1_out, or_1_out, or_2_out, or_3_out, or_4_out, or_5_out;

  Clock clock_1 (.out(clock_1_out));
  and and_1 (and_1_out, A0, L);
  buf or_1 (or_1_out, and_1_out);  // OR_Gate OR_Gate
  nand nand_1 (nand_1_out, L, A0);
  J_K_Flip_Flop j_k_ff_1 (
    .J(or_1_out), .clk(clock_1_out), .K(nand_1_out), .Q(j_k_ff_1_q));  // open: Qn, preset, en, reset
  // AND_Gate and_2 has open pins: in0=j_k_ff_1_q, in1=j_k_ff_2_q, in2=out_5, out=open
  and and_3 (and_3_out, A1, L);
  and and_4 (and_4_out, j_k_ff_1_q, ~L);  // AND_Gate
  and and_5 (and_5_out, ~A1, L);  // AND_Gate
  or or_2 (or_2_out, and_3_out, and_4_out);
  or or_3 (or_3_out, and_4_out, and_5_out);
  J_K_Flip_Flop j_k_ff_2 (
    .J(or_2_out), .clk(clock_1_out), .K(or_3_out), .Q(j_k_ff_2_q));  // open: Qn, preset, en, reset
  and and_6 (and_6_out, j_k_ff_2_q, ~L);  // AND_Gate
  and and_7 (and_7_out, L, A2);
  and and_8 (and_8_out, ~A2, L);  // AND_Gate
  or or_4 (or_4_out, and_6_out, and_7_out);
  J_K_Flip_Flop j_k_ff_3 (.J(or_4_out), .clk(clock_1_out), .K(or_5_out), .Q(out_5));  // open: Qn, preset, en, reset
  or or_5 (or_5_out, and_7_out, and_8_out);
endmodule
