// Logisim project 2023 2.circ as structural Verilog: 1 circuit, main circuit main
module main (
  input  in_1,
  output out_2
);

  wire and_1_out, and_2_out, and_3_out, and_4_out, and_5_out, clock_1_out, d_ff_1_q, d_ff_2_q, d_ff_2_qn,
       d_ff_3_q, d_ff_3_qn, nor_1_out, or_1_out;

  and and_1 (and_1_out, in_1, d_ff_2_q, d_ff_3_qn);
  Clock clock_1 (.out(clock_1_out));
  D_Flip_Flop d_ff_1 (.clk(clock_1_out), .D(and_1_out), .Q(d_ff_1_q));  // open: Qn, preset, en, reset
  D_Flip_Flop d_ff_2 (.clk(clock_1_out), .D(nor_1_out), .Q(d_ff_2_q), .Qn(d_ff_2_qn));  // open: preset, en, reset
  nor nor_1 (nor_1_out, d_ff_1_q, in_1);
  and and_2 (and_2_out, in_1, d_ff_2_q, d_ff_3_q);
  and and_3 (and_3_out, d_ff_1_q, ~in_1);  // AND_Gate
  and and_4 (and_4_out, d_ff_3_q, d_ff_2_qn);
  and and_5 (and_5_out, d_ff_2_qn, in_1);
  or or_1 (or_1_out, and_4_out, and_5_out);
  or or_2 (out_2, and_2_out, and_3_out);
  D_Flip_Flop d_ff_3 (.clk(clock_1_out), .D(or_1_out), .Q(d_ff_3_q), .Qn(d_ff_3_qn));  // open: preset, en, reset
endmodule
