// Logisim project 2023 3 feito por pablo gracias pablo.circ as structural Verilog: 1 circuit, main circuit main
module main (
  input  [1:0] in_1
);

  wire and_1_out, and_2_out, and_3_out, clock_1_out, counter_1_carry, not_1_out, not_2_out, not_3_out;
  wire [1:0] counter_1_q, counter_2_q;

  Clock clock_1 (.out(clock_1_out));
  and and_1 (and_1_out, counter_1_q[0], counter_1_q[1]);
  not not_1 (not_1_out, and_1_out);
  Counter #(.width(2), .max('h3)) counter_1 (
    .load(and_1_out), .D(counter_2_q), .count(not_1_out), .Q(counter_1_q), .carry(counter_1_carry),
    .clk(clock_1_out));  // open: clr
  not not_2 (not_2_out, clock_1_out);
  not not_3 (not_3_out, and_3_out);
  Counter #(.width(2), .max('h3)) counter_2 (
    .load(and_3_out), .D(in_1), .count(not_3_out), .Q(counter_2_q), .clk(and_2_out));  // open: carry, clr
  and and_2 (and_2_out, not_2_out, and_1_out);
  and and_3 (and_3_out, counter_2_q[1], counter_2_q[0]);
endmodule
