// Logisim project 2023 3 non vai.circ as structural Verilog: 1 circuit, main circuit main
module main (
);

  wire and_1_out, clock_1_out, j_k_ff_1_q, j_k_ff_1_qn, j_k_ff_2_q, j_k_ff_2_qn, j_k_ff_3_q, or_1_out,
       or_2_out;

  Clock clock_1 (.out(clock_1_out));
  J_K_Flip_Flop j_k_ff_1 (
    .J(1'b1), .clk(clock_1_out), .K(1'b1), .Q(j_k_ff_1_q), .Qn(j_k_ff_1_qn));  // open: preset, en, reset
  or or_1 (or_1_out, and_1_out, j_k_ff_1_qn);
  J_K_Flip_Flop j_k_ff_2 (
    .J(1'b1), .clk(or_1_out), .K(1'b1), .Q(j_k_ff_2_q), .Qn(j_k_ff_2_qn));  // open: preset, en, reset
  and and_1 (and_1_out, ~j_k_ff_1_q, j_k_ff_2_q, j_k_ff_3_q);  // AND_Gate
  or or_2 (or_2_out, and_1_out, j_k_ff_2_qn);
  J_K_Flip_Flop j_k_ff_3 (.J(1'b1), .clk(or_2_out), .K(1'b1), .Q(j_k_ff_3_q));  // open: Qn, preset, en, reset
endmodule
