// Logisim project 2023 3 si vai.circ as structural Verilog: 1 circuit, main circuit main
module main (
);

  wire _3_out, _5_out, clock_1_out, non5_out, or_1_out, or_2_out, t_ff_1_q, t_ff_1_qn, t_ff_2_q, t_ff_2_qn,
       t_ff_3_qn;

  Clock clock_1 (.out(clock_1_out));
  and _5 (_5_out, ~t_ff_3_qn, ~t_ff_2_q, t_ff_1_q, clock_1_out);  // AND_Gate
  nand non5 (non5_out, ~t_ff_3_qn, ~t_ff_2_q, t_ff_1_q);  // NAND_Gate
  and _3 (_3_out, t_ff_1_q, t_ff_2_q, t_ff_3_qn);
  T_Flip_Flop t_ff_1 (.clk(clock_1_out), .T(non5_out), .Q(t_ff_1_q), .Qn(t_ff_1_qn));  // open: preset, reset, en
  or or_1 (or_1_out, _3_out, _5_out, t_ff_1_qn);
  T_Flip_Flop t_ff_2 (.clk(or_1_out), .T(1'b1), .Q(t_ff_2_q), .Qn(t_ff_2_qn));  // open: preset, reset, en
  T_Flip_Flop t_ff_3 (.clk(or_2_out), .T(1'b1), .Qn(t_ff_3_qn));  // open: Q, preset, reset, en
  or or_2 (or_2_out, _3_out, t_ff_2_qn);
endmodule
