// Logisim project 2023 5.circ as structural Verilog: 1 circuit, main circuit main
module main (
  input  [3:0] in_1,
  input  [3:0] in_2,
  output A_B,
  output A_B_2,
  output A_B_3
);

  wire and_1_out, and_2_out, and_3_out, and_4_out, and_6_out, and_7_out, comparator_1_eq, comparator_1_gt,
       comparator_1_lt, xor_4_out, xor_8_out, xor_9_out;
  wire [2:0] xor_1_out, xor_5_out;

  and and_1 (and_1_out, in_1[0], in_1[1], in_1[2], in_1[3]);
  and and_2 (and_2_out, in_2[0], in_2[1], in_2[2], in_2[3]);
  xor xor_1 (xor_1_out[0], in_1[0], and_1_out);
  xor xor_2 (xor_1_out[1], in_1[1], and_1_out);
  xor xor_3 (xor_1_out[2], in_1[2], and_1_out);
  xor xor_4 (xor_4_out, in_1[3], and_1_out);
  xor xor_5 (xor_5_out[0], in_2[0], and_2_out);
  xor xor_6 (xor_5_out[1], in_2[1], and_2_out);
  xor xor_7 (xor_5_out[2], in_2[2], and_2_out);
  xor xor_8 (xor_8_out, in_2[3], and_2_out);
  Comparator #(.width(3), .mode("unsigned")) comparator_1 (
    .a(xor_1_out), .b(xor_5_out), .gt(comparator_1_gt), .eq(comparator_1_eq), .lt(comparator_1_lt));
  xor xor_9 (xor_9_out, xor_4_out, xor_8_out);
  and and_3 (and_3_out, xor_8_out, xor_9_out);
  and and_4 (and_4_out, comparator_1_gt, ~xor_9_out);  // AND_Gate
  and and_5 (A_B_2, comparator_1_eq, ~xor_9_out);  // AND_Gate
  and and_6 (and_6_out, comparator_1_lt, ~xor_9_out);  // AND_Gate
  and and_7 (and_7_out, xor_9_out, xor_4_out);
  or or_1 (A_B, and_3_out, and_4_out);
  or or_2 (A_B_3, and_6_out, and_7_out);

  // Notes on the sheet:
  //   esta primeira parte é para convertir o 1111 en 0000, porque son o mismo numero
  //   como se inserta \n en logisim
endmodule
