// Logisim project 20_ 4.circ as structural Verilog: 1 circuit, main circuit main
module main (
  input  [3:0] in_1,
  input  [3:0] in_2,
  output [3:0] out_3,
  output [3:0] out_4,
  output out_5
);

  wire and_1_out, and_2_out, clock_1_out, comparator_1_gt, comparator_1_lt, not_1_out, or_1_out, t_ff_1_q;
  wire [3:0] adder_1_out;

  Clock clock_1 (.out(clock_1_out));
  Comparator #(.width(4), .mode("unsigned")) comparator_1 (
    .a(in_1), .b(in_2), .gt(comparator_1_gt), .lt(comparator_1_lt));  // open: eq
  T_Flip_Flop t_ff_1 (.clk(clock_1_out), .T(1'b1), .Q(t_ff_1_q));  // open: Qn, preset, reset, en
  not not_1 (not_1_out, t_ff_1_q);
  and and_1 (and_1_out, in_1[3], comparator_1_gt);
  and and_2 (and_2_out, comparator_1_lt, ~in_2[3]);  // AND_Gate
  Multiplexer #(.width(4)) multiplexer_1 (.in0(in_1), .in1(in_2), .out(out_3), .sel(or_1_out));  // open: en
  or or_1 (or_1_out, and_1_out, and_2_out);
  Adder #(.width(4)) adder_1 (.a(4'b0001), .b(out_3), .out(adder_1_out));  // open: cin, cout
  and and_3 (out_5, out_3[0], out_3[1], not_1_out, out_3[2], ~out_3[3]);  // AND_Gate
  and and_4 (out_4[0], adder_1_out[0], not_1_out);
  and and_5 (out_4[1], adder_1_out[1], not_1_out);
  and and_6 (out_4[2], adder_1_out[2], not_1_out);
  and and_7 (out_4[3], adder_1_out[3], not_1_out);
endmodule
