// Logisim project 20_ 7.circ as structural Verilog: 1 circuit, main circuit main
module main (
  input  P,
  input  S
);

  wire and_1_out, and_2_out, clock_1_out, or_1_out, t_ff_1_q, t_ff_1_qn;

  Clock clock_1 (.out(clock_1_out));
  and and_1 (and_1_out, t_ff_1_qn, P, S);
  and and_2 (and_2_out, ~S, t_ff_1_q);  // AND_Gate
  or or_1 (or_1_out, and_1_out, and_2_out);
  T_Flip_Flop t_ff_1 (.clk(clock_1_out), .T(or_1_out), .Q(t_ff_1_q), .Qn(t_ff_1_qn));  // open: preset, reset, en
endmodule
