// Logisim project comparador c2 pediano en un ejercicio non sei cal.circ as structural Verilog: 1 circuit, main circuit main
module main (
  input  [3:0] in_1,
  input  [3:0] in_2,
  output A_B,
  output A_B_2,
  output A_B_3
);

  wire and_1_out, and_2_out, and_4_out, and_5_out, comparator_1_eq, comparator_1_gt, comparator_1_lt,
       xor_1_out;

  Comparator #(.width(3), .mode("unsigned")) comparator_1 (
    .a(in_1[2:0]), .b(in_2[2:0]), .gt(comparator_1_gt), .eq(comparator_1_eq), .lt(comparator_1_lt));
  xor xor_1 (xor_1_out, in_1[3], in_2[3]);
  and and_1 (and_1_out, in_2[3], xor_1_out);
  and and_2 (and_2_out, comparator_1_gt, ~xor_1_out);  // AND_Gate
  and and_3 (A_B_2, comparator_1_eq, ~xor_1_out);  // AND_Gate
  and and_4 (and_4_out, comparator_1_lt, ~xor_1_out);  // AND_Gate
  and and_5 (and_5_out, xor_1_out, in_1[3]);
  or or_1 (A_B, and_1_out, and_2_out);
  or or_2 (A_B_3, and_4_out, and_5_out);
endmodule
